# Fritzing sketch Connections (saved by Fritzing 0.9.2b)
breadboards: 1

parts:
  Onderdeel1 = Arduino Nano (Rev3.0)
  Onderdeel2 = Bluetooth HC-06
  R1 = Resistor [tolerance=±5% resistance=220 package="0402 [SMD]"]

nets:
  GND: Onderdeel1.GND, Onderdeel2.GND
  N1: Onderdeel1.D10, Onderdeel2.TXD
  N2: Onderdeel1.D11/MOSI, R1.Pin_1
  5V: Onderdeel1.5V, Onderdeel2.VCC
  N3: Onderdeel2.RXD, R1.Pin_0

notes:
  Bluetooth module

// code stored in the sketch: Passthrough_Bluetooth.ino
#include <SoftwareSerial.h>
SoftwareSerial mySerial(10, 11); // RX, TX

String command = ""; // Stores response of the HC-06 Bluetooth device


void setup() {
  // Open serial communications:
  Serial.begin(9600);
  Serial.println("Type AT commands!");
  
  // The HC-06 defaults to 9600 according to the datasheet.
  mySerial.begin(9600);
}

void loop() {
  // Read device output if available.
  if (mySerial.available()) {
    while(mySerial.available()) { // While there is more to be read, keep reading.
      command += (char)mySerial.read();
      delay(10);
    }
    
    Serial.println(command);
    command = ""; // No repeats
  }
  
  // Read user input if available.
  if (Serial.available()){
    delay(10); // The delay is necessary to get this working!
    mySerial.write(Serial.read());
  }
}
